// Logisim project mapa2.circ as structural Verilog: 3 circuits, main circuit main
module main (
  input  [3:0] in_1
);

  wire LogicaEstados_a_2, LogicaEstados_b_2, LogicaEstados_c_2, LogicaEstados_d_2, LogicaEstados_minus_a,
       LogicaEstados_minus_b, LogicaEstados_minus_c, LogicaEstados_minus_d;

  LogicaEstados LogicaEstados (
    .A(in_1[0]), .B(in_1[1]), .C(in_1[2]), .D(in_1[3]), .A_2(LogicaEstados_a_2),
    .minus_A(LogicaEstados_minus_a), .B_2(LogicaEstados_b_2), .minus_B(LogicaEstados_minus_b),
    .C_2(LogicaEstados_c_2), .minus_C(LogicaEstados_minus_c), .D_2(LogicaEstados_d_2),
    .minus_D(LogicaEstados_minus_d));
  LogicaSalida LogicaSalida (
    .C(LogicaEstados_a_2), .minus_C(LogicaEstados_minus_a), .D(LogicaEstados_b_2),
    .minus_D(LogicaEstados_minus_b), .Sb(LogicaEstados_c_2), .Sc(LogicaEstados_minus_c),
    .Sd(LogicaEstados_d_2), .Se(LogicaEstados_minus_d), .Sf(LogicaEstados_a_2), .Sg(LogicaEstados_minus_a));  // open: A, minus_A, B, minus_B, Sa
endmodule

module LogicaEstados (
  input  A,
  input  B,
  input  C,
  input  D,
  output A_2,
  output minus_A,
  output B_2,
  output minus_B,
  output C_2,
  output minus_C,
  output D_2,
  output minus_D
);

  wire BC_out, BD_out, CD_out, clock_1_out, minus_A_B_out, minus_AB_out, minus_AC_out, minus_BD_out;

  Clock clock_1 (.out(clock_1_out));
  J_K_Flip_Flop u_A (.J(A), .clk(clock_1_out), .K(A), .Q(A_2), .Qn(minus_A));  // open: preset, en, reset
  J_K_Flip_Flop u_B (.J(B), .clk(clock_1_out), .K(B), .Q(B_2), .Qn(minus_B));  // open: preset, en, reset
  J_K_Flip_Flop u_C (.J(C), .clk(clock_1_out), .K(C), .Q(C_2), .Qn(minus_C));  // open: preset, en, reset
  J_K_Flip_Flop u_D (.J(D), .clk(clock_1_out), .K(D), .Q(B), .Qn(minus_D));  // open: preset, en, reset
  and BC (BC_out, B_2, C_2);
  and BCD (A, B_2, C_2, B);
  and BD (BD_out, B_2, B);
  and AD (C, A_2, B);
  and CD (CD_out, C_2, B);
  and minus_AC (minus_AC_out, minus_A, C_2);
  and minus_AB (minus_AB_out, minus_A, B_2);
  and minus_BD (minus_BD_out, minus_B, B);
  and minus_A_B (minus_A_B_out, minus_A, minus_B);
  or BD_BC (A, BC_out, BD_out);
  or minus_AC_CD (B, CD_out, minus_AC_out);
  or minus_AB__BD (C, minus_AB_out, minus_BD_out);
  or minus_A_B_C_A (D, minus_A_B_out, C_2, A_2);
  or minus_A_B__C_A (D, minus_A_B_out, minus_C, A_2);

  assign D_2 = B;
endmodule

module LogicaSalida (
  input  A,
  input  minus_A,
  input  B,
  input  minus_B,
  input  C,
  input  minus_C,
  input  D,
  input  minus_D,
  output Sa,
  output Sb,
  output Sc,
  output Sd,
  output Se,
  output Sf,
  output Sg
);

  wire A_B_C_out, AB_out, AD_out, BC_out, BD_out, minus_A_B_C_out, minus_A_B_out, minus_A_BCD_out,
       minus_A_BD_out, minus_A_C_D_out, minus_ACD_out, minus_B_C_D_out, minus_B_CD_out, minus_B_DA_out,
       minus_BCD_out, minus_C_DB_out, minus_CB_out, minus_DAC_out, minus_DC_out;

  and minus_A_B (minus_A_B_out, minus_A, minus_B);
  and minus_BCD (minus_BCD_out, C, minus_B, D);
  and minus_CB (minus_CB_out, B, minus_C);
  and AB (AB_out, A, B);
  and minus_A_B_C (minus_A_B_C_out, minus_A_B_out, minus_C);
  and BD (BD_out, D, B);
  and AD (AD_out, A, D);
  and minus_DC (minus_DC_out, C, minus_D);
  and minus_A_C_D (minus_A_C_D_out, minus_C, minus_A, minus_D);
  and A_B_C (A_B_C_out, minus_C, A, minus_B);
  and minus_A_BCD (minus_A_BCD_out, minus_A_B_out, C, D);
  and minus_DAC (minus_DAC_out, A, C, minus_D);
  and minus_B_C_D (minus_B_C_D_out, minus_B, minus_C, minus_D);
  and minus_C_DB (minus_C_DB_out, minus_D, minus_C, B);
  and minus_A_BD (minus_A_BD_out, minus_A_B_out, D);
  and BC (BC_out, C, B);
  and minus_B_DA (minus_B_DA_out, A, minus_B, minus_D);
  and minus_B_CD (minus_B_CD_out, minus_B, minus_C, D);
  and minus_ACD (minus_ACD_out, C, minus_A, D);
  or minus_A_B____CB____BCD (Sa, A, minus_A_B_out, minus_BCD_out, minus_CB_out);
  or minus_A_B_C___BD___AD___AB____DC (Sb, AB_out, minus_A_B_C_out, BD_out, AD_out, minus_DC_out);
  or B_A_D_C (Sc, D, A, B, C);
  or minus_A_C_D____A_B_C____A_BCD____DAC (Sd, minus_A_C_D_out, A_B_C_out, minus_A_BCD_out, minus_DAC_out);
  or minus_DAC____B_C_D (Se, minus_DAC_out, minus_B_C_D_out);
  or minus_C_DB____A_BD___BC____B_DA (Sf, minus_C_DB_out, minus_A_BD_out, BC_out, minus_B_DA_out);
  or minus_A_B____B_CD____ACD___BC____DAC (Sg, BC_out, minus_DAC_out, minus_ACD_out, minus_A_B_out, minus_B_CD_out);
endmodule
